# Fritzing sketch Amplificateur (saved by Fritzing 0.9.10b)
breadboards: 1

parts:
  R4 = Resistor [tolerance=±5% power=0.25 resistance=220 package=THT]
  R5 = Resistor [tolerance=±5% power=0.25 resistance=220 package=THT]
  Q2 = TRANSISTOR_NPN [package=to-92-ammo]
  D2 = Diode [package=diode-hv]
  U1 = Op Amp [part_number=TL081]
  R6 = Resistor [tolerance=±5% power=0.25W resistance=220 package=THT]
  L1 = Inductor [package="400 mil [THT]"]

nets:
  GND: R4.Pin_0, D2.A, U1.GND, L1.pin_1
  N1: R4.Pin_1, R5.Pin_1, U1.V-
  X: R5.Pin_0, Q2.E, D2.C, R6.Pin_0
  N2: Q2.B, U1.Vout
  30V: Q2.C, U1.VCC
  U: U1.V+
  N3: R6.Pin_1, L1.pin_0

notes:
  bobine
