# Fritzing sketch Modèle complet PD (saved by Fritzing 0.9.10b)
breadboards: 1

parts:
  U1 = Op Amp [part_number=TL081]
  C1 = Ceramic Capacitor [capacitance=100nF voltage=35V package="100 mil [THT, multilayer]"]
  R1 = Resistor [tolerance=±5% power=0.25 resistance=220 package=THT]
  R2 = Resistor [tolerance=±5% power=0.25 resistance=220 package=THT]
  R7 = Resistor [tolerance=±5% power=0.25 resistance=220 package=THT]
  R8 = Resistor [tolerance=±5% power=0.25 resistance=220 package=THT]
  Q3 = TRANSISTOR_NPN [package=to-92-ammo]
  D3 = Diode [package=diode-hv]
  U2 = Op Amp [part_number=TL081]
  R9 = Resistor [tolerance=±5% power=0.25W resistance=220 package=THT]
  L2 = Inductor [package="400 mil [THT]"]
  R16 = Resistor [tolerance=±5% power=0.25 resistance=220 package=THT]
  R17 = Resistor [tolerance=±5% power=0.25 resistance=220 package=THT]
  R18 = Resistor [tolerance=±5% power=0.25 resistance=220 package=THT]
  R19 = Resistor [tolerance=±5% power=0.25 resistance=220 package=THT]
  U3 = Op Amp [part_number=TL081]
  J1 = Infrared Proximity Sensor [distance_to_obstacle=50%]

nets:
  N1: U1.V-, C1.1, R1.Pin_0, R2.Pin_1
  GND: U1.V+, U1.GND, R7.Pin_0, D3.A, U2.GND, L2.pin_1, R16.Pin_0, U3.GND, J1.GND
  N2: U1.Vout, R1.Pin_1, U2.V+
  30V: U1.VCC, Q3.C, U2.VCC, U3.VCC
  N3: C1.0, R2.Pin_0, R19.Pin_0, U3.Vout
  N4: R7.Pin_1, R8.Pin_1, U2.V-
  N5: R8.Pin_0, Q3.E, D3.C, R9.Pin_0
  N6: Q3.B, U2.Vout
  N7: R9.Pin_1, L2.pin_0
  N8: R16.Pin_1, R17.Pin_0, U3.V+
  N9: R17.Pin_1, J1.Vout
  N10: R18.Pin_0, R19.Pin_1, U3.V-
  C: R18.Pin_1
  5V: J1.Vcc

notes:
  bobine
  Ym
  ɛ
  U
  Y
  capteur
