# Fritzing sketch Régulateur PID (saved by Fritzing 0.9.10b)
breadboards: 1

parts:
  U1 = Op Amp [part_number=TL081]
  C1 = Ceramic Capacitor [capacitance=100nF voltage=35V package="100 mil [THT, multilayer]"]
  R1 = Resistor [tolerance=±5% power=0.25 resistance=220 package=THT]
  R2 = Resistor [tolerance=±5% power=0.25 resistance=220 package=THT]
  C2 = Ceramic Capacitor [capacitance=100nF voltage=35V package="100 mil [THT, multilayer]"]

nets:
  N1: U1.V-, C1.1, R1.Pin_0, R2.Pin_1, C2.0
  GND: U1.V+, U1.GND
  U: U1.Vout, R1.Pin_1, C2.1
  30V: U1.VCC
  ɛ: C1.0, R2.Pin_0
