# Fritzing sketch coucou (saved by Fritzing 0.9.10b)

parts:
  R1 = Resistor [tolerance=±5% power=0.25 resistance=220 package=THT]
  V1 = DC Power [voltage=5]
  Q1 = TRANSISTOR_NPN [package=to-92-ammo]
  D1 = Diode [package=diode-hv]
  R3 = Resistor [tolerance=±5% power=0.25 resistance=220 package=THT]
  L1 = Inductor [package="400 mil [THT]"]
  R4 = Resistor [tolerance=±5% power=0.25 resistance=220 package=THT]
  R5 = Resistor [tolerance=±5% power=0.25 resistance=220 package=THT]
  Q2 = TRANSISTOR_NPN [package=to-92-ammo]
  D2 = Diode [package=diode-hv]
  L2 = Inductor [package="400 mil [THT]"]
  R6 = Resistor [tolerance=±5% power=0.25 resistance=220 package=THT]
  C1 = Ceramic Capacitor [capacitance="100 nF" voltage=35V package="1206 [SMD, multilayer]"]
  R7 = Resistor [tolerance=±5% power=0.25 resistance=220 package=THT]
  V6 = DC Power [voltage=5]
  R8 = Resistor [tolerance=±5% power=0.25 resistance=220 package=THT]
  R9 = Resistor [tolerance=±5% power=0.25 resistance=220 package=THT]
  R10 = Resistor [tolerance=±5% power=0.25 resistance=220 package=THT]
  R11 = Resistor [tolerance=±5% power=0.25 resistance=220 package=THT]
  Q3 = TRANSISTOR_NPN [package=to-92-ammo]
  D3 = Diode [package=diode-hv]
  L3 = Inductor [package="400 mil [THT]"]
  C2 = Ceramic Capacitor [capacitance="100 nF" voltage=35V package="1206 [SMD, multilayer]"]
  R12 = Resistor [tolerance=±5% power=0.25 resistance=220 package=THT]
  R13 = Resistor [tolerance=±5% power=0.25 resistance=220 package=THT]
  V9 = DC Power [voltage=5]
  R14 = Resistor [tolerance=±5% power=0.25 resistance=220 package=THT]
  R15 = Resistor [tolerance=±5% power=0.25 resistance=220 package=THT]
  R16 = Resistor [tolerance=±5% power=0.25 resistance=220 package=THT]
  R17 = Resistor [tolerance=±5% power=0.25 resistance=220 package=THT]
  R18 = Resistor [tolerance=±5% power=0.25 resistance=220 package=THT]
  R19 = Resistor [tolerance=±5% power=0.25 resistance=220 package=THT]
  Q4 = TRANSISTOR_NPN [package=to-92-ammo]
  D4 = Diode [package=diode-hv]
  L4 = Inductor [package="400 mil [THT]"]
  C3 = Ceramic Capacitor [capacitance="100 nF" voltage=35V package="1206 [SMD, multilayer]"]
  V13 = DC Power [voltage=5]
  C4 = Ceramic Capacitor [capacitance="100 nF" voltage=35V package="1206 [SMD, multilayer]"]
  R20 = Resistor [tolerance=±5% power=0.25 resistance=220 package=THT]
  R21 = Resistor [tolerance=±5% power=0.25 resistance=220 package=THT]
  R22 = Resistor [tolerance=±5% power=0.25 resistance=220 package=THT]
  R23 = Resistor [tolerance=±5% power=0.25 resistance=220 package=THT]
  R24 = Resistor [tolerance=±5% power=0.25 resistance=220 package=THT]
  R25 = Resistor [tolerance=±5% power=0.25 resistance=220 package=THT]
  R26 = Resistor [tolerance=±5% power=0.25 resistance=220 package=THT]
  R27 = Resistor [tolerance=±5% power=0.25 resistance=220 package=THT]
  Q5 = TRANSISTOR_NPN [package=to-92-ammo]
  D5 = Diode [package=diode-hv]
  L5 = Inductor [package="400 mil [THT]"]
  C5 = Ceramic Capacitor [capacitance="100 nF" voltage=35V package="1206 [SMD, multilayer]"]
  V17 = DC Power [voltage=5]
  C6 = Ceramic Capacitor [capacitance="100 nF" voltage=35V package="1206 [SMD, multilayer]"]
  LM2 = LM741 [part_number=LM741 package="DIP (Dual Inline) [THT]"]
  LM10 = LM741 [part_number=LM741 package="DIP (Dual Inline) [THT]"]
  LM1 = LM741 [part_number=LM741 package="DIP (Dual Inline) [THT]"]
  LM7 = LM741 [part_number=LM741 package="DIP (Dual Inline) [THT]"]
  LM4 = LM741 [part_number=LM741 package="DIP (Dual Inline) [THT]"]
  LM3 = LM741 [part_number=LM741 package="DIP (Dual Inline) [THT]"]
  LM8 = LM741 [part_number=LM741 package="DIP (Dual Inline) [THT]"]
  LM11 = LM741 [part_number=LM741 package="DIP (Dual Inline) [THT]"]
  LM9 = LM741 [part_number=LM741 package="DIP (Dual Inline) [THT]"]
  LM5 = LM741 [part_number=LM741 package="DIP (Dual Inline) [THT]"]
  LM6 = LM741 [part_number=LM741 package="DIP (Dual Inline) [THT]"]

nets:
  GND: R1.Pin_0, V1.V-, D1.A, L1.pin_1, R4.Pin_0, D2.A, L2.pin_1, V6.V-, R9.Pin_0, D3.A, L3.pin_1, V9.V-, R15.Pin_0, R18.Pin_0, D4.A, L4.pin_1, V13.V-, R23.Pin_0, R25.Pin_0, D5.A, L5.pin_1, V17.V-, LM2.GND, LM10.GND, LM1.GND, LM7.GND, LM4.GND, LM3.+, LM3.GND, LM8.+, LM8.GND, LM11.GND, LM9.+, LM9.GND, LM5.+, LM5.GND, LM6.GND
  N1: R1.Pin_1, R3.Pin_1, LM1.-
  N2: V1.V+, LM1.+
  N3: Q1.E, D1.C, R3.Pin_0, L1.pin_0
  N4: Q1.B, LM1.Vout
  30V: Q1.C, Q2.C, Q3.C, Q4.C, Q5.C, LM2.VCC, LM10.VCC, LM1.VCC, LM7.VCC, LM4.VCC, LM3.VCC, LM8.VCC, LM11.VCC, LM9.VCC, LM5.VCC, LM6.VCC
  N5: R4.Pin_1, R5.Pin_1, LM2.-
  N6: R5.Pin_0, Q2.E, D2.C, L2.pin_0
  N7: Q2.B, LM2.Vout
  N8: R6.Pin_0, C1.1, R7.Pin_1, LM3.-
  N9: R6.Pin_1, C1.0, V6.V+
  N10: R7.Pin_0, LM2.+, LM3.Vout
  N11: R8.Pin_0, R10.Pin_1, C2.1, LM5.-
  N12: R8.Pin_1, C2.0, R12.Pin_0, LM6.Vout
  N13: R9.Pin_1, R11.Pin_1, LM4.-
  N14: R10.Pin_0, LM4.+, LM5.Vout
  N15: R11.Pin_0, Q3.E, D3.C, L3.pin_0, R14.Pin_1
  N16: Q3.B, LM4.Vout
  N17: R12.Pin_1, R13.Pin_0, LM6.-
  N18: R13.Pin_1, V9.V+
  N19: R14.Pin_0, R15.Pin_1, LM6.+
  N20: R16.Pin_0, R17.Pin_1, C3.1, C4.0, LM8.-
  N21: R16.Pin_1, C3.0, V13.V+
  N22: R17.Pin_0, C4.1, LM7.+, LM8.Vout
  N23: R18.Pin_1, R19.Pin_1, LM7.-
  N24: R19.Pin_0, Q4.E, D4.C, L4.pin_0
  N25: Q4.B, LM7.Vout
  N26: R20.Pin_0, R26.Pin_1, C5.1, C6.0, LM9.-
  N27: R20.Pin_1, R22.Pin_0, C5.0, LM11.Vout
  N28: R21.Pin_0, R23.Pin_1, LM11.+
  N29: R21.Pin_1, R27.Pin_0, Q5.E, D5.C, L5.pin_0
  N30: R22.Pin_1, R24.Pin_0, LM11.-
  N31: R24.Pin_1, V17.V+
  N32: R25.Pin_1, R27.Pin_1, LM10.-
  N33: R26.Pin_0, C6.1, LM10.+, LM9.Vout
  N34: Q5.B, LM10.Vout

notes:
  Vout
  Montage Ampli Classique
  Montage Ampli + Correcteur PD
  Montage Ampli + Correcteur PD + Retour (dans comparateur)
  Espilon
  V1
  C
  Yr
  Vout / Y
  Montage Ampli + Correcteur PID
  Montage Ampli + Correcteur PID + Retour (dans comparateur)
  bobine

custom parts:
  LM741: This is a single Op Amp DIP.
