# Fritzing sketch coucou (saved by Fritzing 0.9.10b)

parts:
  LM1 = LM741 [part_number=LM741 package="DIP (Dual Inline) [THT]"]
  R1 = Resistor [tolerance=±5% power=0.25 resistance=220 package=THT]
  V1 = DC Power [voltage=5]
  Q1 = TRANSISTOR_NPN [package=to-92-ammo]
  D1 = Diode [package=diode-hv]
  R3 = Resistor [tolerance=±5% power=0.25 resistance=220 package=THT]
  L1 = Inductor [package="400 mil [THT]"]
  LM2 = LM741 [part_number=LM741 package="DIP (Dual Inline) [THT]"]
  R4 = Resistor [tolerance=±5% power=0.25 resistance=220 package=THT]
  R5 = Resistor [tolerance=±5% power=0.25 resistance=220 package=THT]
  Q2 = TRANSISTOR_NPN [package=to-92-ammo]
  D2 = Diode [package=diode-hv]
  L2 = Inductor [package="400 mil [THT]"]
  R6 = Resistor [tolerance=±5% power=0.25 resistance=220 package=THT]
  C1 = Ceramic Capacitor [capacitance="100 nF" voltage=35V package="1206 [SMD, multilayer]"]
  LM3 = LM741 [part_number=LM741 package="DIP (Dual Inline) [THT]"]
  R7 = Resistor [tolerance=±5% power=0.25 resistance=220 package=THT]
  V6 = DC Power [voltage=5]
  LM4 = LM741 [part_number=LM741 package="DIP (Dual Inline) [THT]"]
  LM5 = LM741 [part_number=LM741 package="DIP (Dual Inline) [THT]"]
  R8 = Resistor [tolerance=±5% power=0.25 resistance=220 package=THT]
  R9 = Resistor [tolerance=±5% power=0.25 resistance=220 package=THT]
  R10 = Resistor [tolerance=±5% power=0.25 resistance=220 package=THT]
  R11 = Resistor [tolerance=±5% power=0.25 resistance=220 package=THT]
  Q3 = TRANSISTOR_NPN [package=to-92-ammo]
  D3 = Diode [package=diode-hv]
  L3 = Inductor [package="400 mil [THT]"]
  C2 = Ceramic Capacitor [capacitance="100 nF" voltage=35V package="1206 [SMD, multilayer]"]
  LM6 = LM741 [part_number=LM741 package="DIP (Dual Inline) [THT]"]
  R12 = Resistor [tolerance=±5% power=0.25 resistance=220 package=THT]
  R13 = Resistor [tolerance=±5% power=0.25 resistance=220 package=THT]
  V9 = DC Power [voltage=5]
  R14 = Resistor [tolerance=±5% power=0.25 resistance=220 package=THT]
  R15 = Resistor [tolerance=±5% power=0.25 resistance=220 package=THT]
  LM7 = LM741 [part_number=LM741 package="DIP (Dual Inline) [THT]"]
  LM8 = LM741 [part_number=LM741 package="DIP (Dual Inline) [THT]"]
  R16 = Resistor [tolerance=±5% power=0.25 resistance=220 package=THT]
  R17 = Resistor [tolerance=±5% power=0.25 resistance=220 package=THT]
  R18 = Resistor [tolerance=±5% power=0.25 resistance=220 package=THT]
  R19 = Resistor [tolerance=±5% power=0.25 resistance=220 package=THT]
  Q4 = TRANSISTOR_NPN [package=to-92-ammo]
  D4 = Diode [package=diode-hv]
  L4 = Inductor [package="400 mil [THT]"]
  C3 = Ceramic Capacitor [capacitance="100 nF" voltage=35V package="1206 [SMD, multilayer]"]
  V13 = DC Power [voltage=5]
  C4 = Ceramic Capacitor [capacitance="100 nF" voltage=35V package="1206 [SMD, multilayer]"]
  LM9 = LM741 [part_number=LM741 package="DIP (Dual Inline) [THT]"]
  LM10 = LM741 [part_number=LM741 package="DIP (Dual Inline) [THT]"]
  LM11 = LM741 [part_number=LM741 package="DIP (Dual Inline) [THT]"]
  R20 = Resistor [tolerance=±5% power=0.25 resistance=220 package=THT]
  R21 = Resistor [tolerance=±5% power=0.25 resistance=220 package=THT]
  R22 = Resistor [tolerance=±5% power=0.25 resistance=220 package=THT]
  R23 = Resistor [tolerance=±5% power=0.25 resistance=220 package=THT]
  R24 = Resistor [tolerance=±5% power=0.25 resistance=220 package=THT]
  R25 = Resistor [tolerance=±5% power=0.25 resistance=220 package=THT]
  R26 = Resistor [tolerance=±5% power=0.25 resistance=220 package=THT]
  R27 = Resistor [tolerance=±5% power=0.25 resistance=220 package=THT]
  Q5 = TRANSISTOR_NPN [package=to-92-ammo]
  D5 = Diode [package=diode-hv]
  L5 = Inductor [package="400 mil [THT]"]
  C5 = Ceramic Capacitor [capacitance="100 nF" voltage=35V package="1206 [SMD, multilayer]"]
  V17 = DC Power [voltage=5]
  C6 = Ceramic Capacitor [capacitance="100 nF" voltage=35V package="1206 [SMD, multilayer]"]

nets:
  N1: LM1.pin2, R1.Pin_1, R3.Pin_1
  N2: LM1.pin3, V1.V+
  GND: LM1.pin4, R1.Pin_0, V1.V-, D1.A, L1.pin_1, LM2.pin4, R4.Pin_0, D2.A, L2.pin_1, LM3.pin3, LM3.pin4, V6.V-, LM4.pin4, LM5.pin3, LM5.pin4, R9.Pin_0, D3.A, L3.pin_1, LM6.pin4, V9.V-, R15.Pin_0, LM7.pin4, LM8.pin3, LM8.pin4, R18.Pin_0, D4.A, L4.pin_1, V13.V-, LM9.pin3, LM9.pin4, LM10.pin4, LM11.pin4, R23.Pin_0, R25.Pin_0, D5.A, L5.pin_1, V17.V-
  N3: LM1.pin6, Q1.B
  30V: LM1.pin7, Q1.C, LM2.pin7, Q2.C, LM3.pin7, LM4.pin7, LM5.pin7, Q3.C, LM6.pin7, LM7.pin7, LM8.pin7, Q4.C, LM9.pin7, LM10.pin7, LM11.pin7, Q5.C
  N4: Q1.E, D1.C, R3.Pin_0, L1.pin_0
  N5: LM2.pin2, R4.Pin_1, R5.Pin_1
  N6: LM2.pin3, LM3.pin6, R7.Pin_0
  N7: LM2.pin6, Q2.B
  N8: R5.Pin_0, Q2.E, D2.C, L2.pin_0
  N9: R6.Pin_0, C1.1, LM3.pin2, R7.Pin_1
  N10: R6.Pin_1, C1.0, V6.V+
  N11: LM4.pin2, R9.Pin_1, R11.Pin_1
  N12: LM4.pin3, LM5.pin6, R10.Pin_0
  N13: LM4.pin6, Q3.B
  N14: LM5.pin2, R8.Pin_0, R10.Pin_1, C2.1
  N15: R8.Pin_1, C2.0, LM6.pin6, R12.Pin_0
  N16: R11.Pin_0, Q3.E, D3.C, L3.pin_0, R14.Pin_1
  N17: LM6.pin2, R12.Pin_1, R13.Pin_0
  N18: LM6.pin3, R14.Pin_0, R15.Pin_1
  N19: R13.Pin_1, V9.V+
  N20: LM7.pin2, R18.Pin_1, R19.Pin_1
  N21: LM7.pin3, LM8.pin6, R17.Pin_0, C4.1
  N22: LM7.pin6, Q4.B
  N23: LM8.pin2, R16.Pin_0, R17.Pin_1, C3.1, C4.0
  N24: R16.Pin_1, C3.0, V13.V+
  N25: R19.Pin_0, Q4.E, D4.C, L4.pin_0
  N26: LM9.pin2, R20.Pin_0, R26.Pin_1, C5.1, C6.0
  N27: LM9.pin6, LM10.pin3, R26.Pin_0, C6.1
  N28: LM10.pin2, R25.Pin_1, R27.Pin_1
  N29: LM10.pin6, Q5.B
  N30: LM11.pin2, R22.Pin_1, R24.Pin_0
  N31: LM11.pin3, R21.Pin_0, R23.Pin_1
  N32: LM11.pin6, R20.Pin_1, R22.Pin_0, C5.0
  N33: R21.Pin_1, R27.Pin_0, Q5.E, D5.C, L5.pin_0
  N34: R24.Pin_1, V17.V+

notes:
  Vout
  Montage Ampli Classique
  Montage Ampli + Correcteur PD
  Montage Ampli + Correcteur PD + Retour (dans comparateur)
  Espilon
  V1
  C
  Yr
  Vout / Y
  Montage Ampli + Correcteur PID
  Montage Ampli + Correcteur PID + Retour (dans comparateur)

custom parts:
  LM741: This is a single Op Amp DIP.
